// Logisim project CPU_8b.circ as structural Verilog
module Somador_Completo (
  input  A,
  input  B,
  input  Cin,
  output out_4,
  output out_5
);

  wire and_1_out, and_2_out, and_3_out, xor_1_out;

  xor xor_1 (xor_1_out, A, B);
  and and_1 (and_1_out, A, Cin);
  and and_2 (and_2_out, A, B);
  and and_3 (and_3_out, B, Cin);
  xor xor_2 (out_4, xor_1_out, Cin);
  or or_1 (out_5, and_1_out, and_2_out, and_3_out);
endmodule

module Somador_8b (
  input  Cin,
  input  [7:0] A,
  input  [7:0] B,
  output [7:0] S,
  output Cout
);

  wire somador_completo_1_out_5, somador_completo_2_out_5, somador_completo_3_out_5,
       somador_completo_4_out_5, somador_completo_5_out_5, somador_completo_6_out_5, somador_completo_7_out_5;

  Somador_Completo somador_completo_1 (.A(A[0]), .B(B[0]), .Cin(Cin), .out_5(somador_completo_1_out_5), .out_4(S[0]));
  Somador_Completo somador_completo_2 (
    .A(A[1]), .B(B[1]), .Cin(somador_completo_1_out_5), .out_5(somador_completo_2_out_5), .out_4(S[1]));
  Somador_Completo somador_completo_3 (
    .A(A[2]), .B(B[2]), .Cin(somador_completo_2_out_5), .out_5(somador_completo_3_out_5), .out_4(S[2]));
  Somador_Completo somador_completo_4 (
    .A(A[3]), .B(B[3]), .Cin(somador_completo_3_out_5), .out_5(somador_completo_4_out_5), .out_4(S[3]));
  Somador_Completo somador_completo_5 (
    .A(A[4]), .B(B[4]), .Cin(somador_completo_4_out_5), .out_5(somador_completo_5_out_5), .out_4(S[4]));
  Somador_Completo somador_completo_6 (
    .A(A[5]), .B(B[5]), .Cin(somador_completo_5_out_5), .out_5(somador_completo_6_out_5), .out_4(S[5]));
  Somador_Completo somador_completo_7 (
    .A(A[6]), .B(B[6]), .Cin(somador_completo_6_out_5), .out_5(somador_completo_7_out_5), .out_4(S[6]));
  Somador_Completo somador_completo_8 (.A(A[7]), .B(B[7]), .Cin(somador_completo_7_out_5), .out_5(Cout), .out_4(S[7]));
endmodule
